# Fritzing sketch Careers in Medicine Wiring Schematic (saved by Fritzing 0.9.8b)
breadboards: 1

parts:
  Mod1 = Raspberry Pi 4B
  Switch_1 = D2F-FL Omron Snap Action Limit Switch with Level
  Switch_3 = D2F-FL Omron Snap Action Limit Switch with Level
  Swtich_2 = D2F-FL Omron Snap Action Limit Switch with Level
  Switch_4 = D2F-FL Omron Snap Action Limit Switch with Level
  Switch_5 = D2F-FL Omron Snap Action Limit Switch with Level
  Switch_1_LED = LEDs [package=led10mm]
  Switch_2_LED = LEDs [package=led10mm]
  Switch_3_LED = LEDs [package=led10mm]
  Switch_4_LED = LEDs [package=led10mm]
  Switch_5_LED = LEDs [package=led10mm]
  RGB_LED_Ring_5 = LEDs [package=led10mm]
  RGB_LED_Ring_4 = LEDs [package=led10mm]
  RGB_LED_Ring_3 = LEDs [package=led10mm]
  RGB_LED_Ring_2 = LEDs [package=led10mm]
  RGB_LED_Ring_1 = LEDs [package=led10mm]
  12VDC_Power_Supply = DC Power [voltage=12V]
  DPDT_Relay_5 = DPDT Relay [chip_label=Relay package="DIP (Dual Inline) [THT]"]
  DPDT_Relay_4 = DPDT Relay [chip_label=Relay package="DIP (Dual Inline) [THT]"]
  DPDT_Relay_3 = DPDT Relay [chip_label=Relay package="DIP (Dual Inline) [THT]"]
  DPDT_Relay_2 = DPDT Relay [chip_label=Relay package="DIP (Dual Inline) [THT]"]
  DPDT_Relay_1 = DPDT Relay [chip_label=Relay package="DIP (Dual Inline) [THT]"]
  DPDT_Relay_6 = DPDT Relay [chip_label=Relay package="DIP (Dual Inline) [THT]"]
  DPDT_Relay_7 = DPDT Relay [chip_label=Relay package="DIP (Dual Inline) [THT]"]
  DPDT_Relay_8 = DPDT Relay [chip_label=Relay package="DIP (Dual Inline) [THT]"]

nets:
  N1: Mod1.GPIO2, Switch_1.NO
  N2: Mod1.GPIO3, Swtich_2.NO
  N3: Mod1.GND, Switch_1.COM, Switch_3.COM, Swtich_2.COM, Switch_4.COM, Switch_5.COM, DPDT_Relay_5.pin8, DPDT_Relay_4.pin8, DPDT_Relay_3.pin8, DPDT_Relay_2.pin8, DPDT_Relay_1.pin8, DPDT_Relay_6.pin8, DPDT_Relay_7.pin8, DPDT_Relay_8.pin8
  N4: Mod1.GPIO4, Switch_3.NO
  N5: Mod1.GPIO17, Switch_4.NO
  N6: Mod1.GPIO27, Switch_5.NO
  N7: Mod1.GPIO11, DPDT_Relay_6.pin1, DPDT_Relay_7.pin1, DPDT_Relay_8.pin1
  N8: Mod1.GPIO5, DPDT_Relay_1.pin1
  N9: Mod1.GPIO6, DPDT_Relay_2.pin1
  N10: Mod1.GPIO13, DPDT_Relay_3.pin1
  N11: Mod1.GPIO19, DPDT_Relay_4.pin1
  N12: Mod1.GPIO26, DPDT_Relay_5.pin1
  N13: Switch_1_LED.C, DPDT_Relay_1.pin6
  N14: Switch_1_LED.A, Switch_2_LED.A, Switch_3_LED.A, Switch_4_LED.A, Switch_5_LED.A, RGB_LED_Ring_5.A, RGB_LED_Ring_4.A, RGB_LED_Ring_3.A, RGB_LED_Ring_2.A, RGB_LED_Ring_1.A, 12VDC_Power_Supply.V+
  N15: Switch_2_LED.C, DPDT_Relay_2.pin6
  N16: Switch_3_LED.C, DPDT_Relay_3.pin6
  N17: Switch_4_LED.C, DPDT_Relay_4.pin6
  N18: Switch_5_LED.C, DPDT_Relay_5.pin6
  N19: RGB_LED_Ring_5.C, DPDT_Relay_5.pin3, DPDT_Relay_8.pin4
  N20: RGB_LED_Ring_4.C, DPDT_Relay_4.pin3, DPDT_Relay_7.pin5
  N21: RGB_LED_Ring_3.C, DPDT_Relay_3.pin3, DPDT_Relay_7.pin4
  N22: RGB_LED_Ring_2.C, DPDT_Relay_2.pin3, DPDT_Relay_6.pin5
  N23: RGB_LED_Ring_1.C, DPDT_Relay_1.pin3, DPDT_Relay_6.pin4
  N24: 12VDC_Power_Supply.V-, DPDT_Relay_5.pin2, DPDT_Relay_5.pin7, DPDT_Relay_4.pin2, DPDT_Relay_4.pin7, DPDT_Relay_3.pin2, DPDT_Relay_3.pin7, DPDT_Relay_2.pin2, DPDT_Relay_2.pin7, DPDT_Relay_1.pin2, DPDT_Relay_1.pin7, DPDT_Relay_6.pin7

custom parts:
  D2F-FL Omron Snap Action Limit Switch with Level: Snap action switch with stainless steel lever.
  DPDT Relay: DIP DPDT Relay (Double Pole Double Throw)
